// Digital circuit ALU.dig as structural Verilog
module ALU (
);

  wire adder_subtractor_1_c_8, adder_subtractor_1_f, adder_subtractor_1_stc, adder_subtractor_1_stf,
       comparator_1_eq, comparator_2_eq, comparator_3_eq, comparator_4_eq, comparator_5_eq, comparator_6_eq,
       comparator_7_eq, comparator_8_eq, comparator_9_eq, comparator_10_eq, comparator_11_eq,
       comparator_12_eq, comparator_13_eq, comparator_14_eq, comparator_15_eq, comparator_16_eq,
       comparator_17_eq, comparator_18_eq, comparator_19_eq, comparator_20_eq, comparator_22_eq,
       comparator_23_eq, comparator_24_eq, comparator_25_eq, comparator_26_eq, comparator_27_eq,
       comparator_28_eq, comparator_29_eq, flag_register_1_c, incrementor_1_q_s, or_1_out,
       shift_register_1_p2;
  wire [7:0] register_1_q, register_1_val, register_2_val, shift_register_1_p1, undriven_29;
  wire [7:1] undriven, undriven_2, undriven_3, undriven_4, undriven_5, undriven_6, undriven_7, undriven_8,
       undriven_9, undriven_10, undriven_11, undriven_12, undriven_13, undriven_14, undriven_15, undriven_16,
       undriven_17, undriven_18, undriven_19, undriven_20, undriven_21, undriven_22, undriven_23,
       undriven_24, undriven_25, undriven_26, undriven_27, undriven_28;

  Comparator #(.Bits(8)) comparator_1 (.a(undriven_29), .b({undriven_23, 1'b1}), .eq(comparator_1_eq));  // open: gt, lt
  Comparator #(.Bits(8)) comparator_2 (.a(undriven_29), .b({undriven_24, 1'b1}), .eq(comparator_2_eq));  // open: gt, lt
  Comparator #(.Bits(8)) comparator_3 (.a(undriven_29), .b({undriven_25, 1'b1}), .eq(comparator_3_eq));  // open: gt, lt
  Comparator #(.Bits(8)) comparator_4 (.a(undriven_29), .b({undriven_26, 1'b1}), .eq(comparator_4_eq));  // open: gt, lt
  Comparator #(.Bits(8)) comparator_5 (.a(undriven_29), .b({undriven_27, 1'b1}), .eq(comparator_5_eq));  // open: gt, lt
  Comparator #(.Bits(8)) comparator_6 (.a(undriven_29), .b({undriven_28, 1'b1}), .eq(comparator_6_eq));  // open: gt, lt
  or or_1 (or_1_out, comparator_5_eq, incrementor_1_q_s);
  Register register_1 (
    .D(shift_register_1_p1), .STR(comparator_1_eq), .LD(comparator_2_eq), .CLK(shift_register_1_p2),
    .VAL(register_1_val), .Q(register_1_q));
  Register register_2 (
    .D(shift_register_1_p1), .STR(comparator_3_eq), .LD(comparator_4_eq), .CLK(shift_register_1_p2),
    .VAL(register_2_val), .Q(register_1_q));
  Register register_3 (
    .D(shift_register_1_p1), .STR(or_1_out), .LD(comparator_6_eq), .CLK(shift_register_1_p2),
    .VAL(register_2_val), .Q(register_1_q));
  Comparator #(.Bits(8)) comparator_7 (.a(undriven_29), .b({undriven, 1'b1}), .eq(comparator_7_eq));  // open: gt, lt
  Comparator #(.Bits(8)) comparator_8 (.a(undriven_29), .b({undriven_2, 1'b1}), .eq(comparator_8_eq));  // open: gt, lt
  Comparator #(.Bits(8)) comparator_9 (.a(undriven_29), .b({undriven_3, 1'b1}), .eq(comparator_9_eq));  // open: gt, lt
  Comparator #(.Bits(8)) comparator_10 (
    .a(undriven_29), .b({undriven_4, 1'b1}), .eq(comparator_10_eq));  // open: gt, lt
  Comparator #(.Bits(8)) comparator_11 (
    .a(undriven_29), .b({undriven_5, 1'b1}), .eq(comparator_11_eq));  // open: gt, lt
  Comparator #(.Bits(8)) comparator_12 (
    .a(undriven_29), .b({undriven_6, 1'b1}), .eq(comparator_12_eq));  // open: gt, lt
  Comparator #(.Bits(8)) comparator_13 (
    .a(undriven_29), .b({undriven_7, 1'b1}), .eq(comparator_13_eq));  // open: gt, lt
  Comparator #(.Bits(8)) comparator_14 (
    .a(undriven_29), .b({undriven_8, 1'b1}), .eq(comparator_14_eq));  // open: gt, lt
  Comparator #(.Bits(8)) comparator_15 (
    .a(undriven_29), .b({undriven_9, 1'b1}), .eq(comparator_15_eq));  // open: gt, lt
  Comparator #(.Bits(8)) comparator_16 (
    .a(undriven_29), .b({undriven_10, 1'b1}), .eq(comparator_16_eq));  // open: gt, lt
  Comparator #(.Bits(8)) comparator_17 (
    .a(undriven_29), .b({undriven_11, 1'b1}), .eq(comparator_17_eq));  // open: gt, lt
  Comparator #(.Bits(8)) comparator_18 (
    .a(undriven_29), .b({undriven_12, 1'b1}), .eq(comparator_18_eq));  // open: gt, lt
  Comparator #(.Bits(8)) comparator_19 (
    .a(undriven_29), .b({undriven_13, 1'b1}), .eq(comparator_19_eq));  // open: gt, lt
  Comparator #(.Bits(8)) comparator_20 (
    .a(undriven_29), .b({undriven_14, 1'b1}), .eq(comparator_20_eq));  // open: gt, lt
  Flag_Register flag_register_1 (
    .DAT(shift_register_1_p1), .C_8(adder_subtractor_1_c_8), .F(adder_subtractor_1_f),
    .STC(adder_subtractor_1_stc), .STF(adder_subtractor_1_stf), .STA(comparator_7_eq), .LDC(comparator_8_eq),
    .LDF(comparator_9_eq), .LDA(comparator_10_eq), .CLK(shift_register_1_p2), .Q(register_1_q),
    .C(flag_register_1_c));
  Adder_Subtractor adder_subtractor_1 (
    .C_in(flag_register_1_c), .A(register_1_val), .B(register_2_val), .ADD(comparator_11_eq),
    .ADC(comparator_12_eq), .SUB(comparator_13_eq), .CLK(shift_register_1_p2), .Q(register_1_q),
    .C_8(adder_subtractor_1_c_8), .F(adder_subtractor_1_f), .STC(adder_subtractor_1_stc),
    .STF(adder_subtractor_1_stf));
  Incrementor incrementor_1 (
    .C(register_2_val), .INC(comparator_14_eq), .DEC(comparator_15_eq), .CLK(shift_register_1_p2),
    .Q(register_1_q), .C_8(adder_subtractor_1_c_8), .F(adder_subtractor_1_f), .STC(adder_subtractor_1_stc),
    .STF(adder_subtractor_1_stf), .Q_S(incrementor_1_q_s));
  Comparator comparator_21 (
    .A(register_1_val), .B(register_2_val), .CMP_bigger(comparator_16_eq), .CMP_equal(comparator_17_eq),
    .CMP_smaller(comparator_18_eq), .CLK(shift_register_1_p2), .Q(register_1_q));
  // Shift_Register shift_register_1: pin names not known; wires that end beside it: shift_register_1_p1, shift_register_1_p2, register_1_val, shift_register_1_p1, comparator_19_eq, comparator_20_eq, shift_register_1_p2, register_1_q, register_1_q
  Comparator #(.Bits(8)) comparator_22 (
    .a(undriven_29), .b({undriven_15, 1'b1}), .eq(comparator_22_eq));  // open: gt, lt
  Comparator #(.Bits(8)) comparator_23 (
    .a(undriven_29), .b({undriven_16, 1'b1}), .eq(comparator_23_eq));  // open: gt, lt
  Comparator #(.Bits(8)) comparator_24 (
    .a(undriven_29), .b({undriven_17, 1'b1}), .eq(comparator_24_eq));  // open: gt, lt
  Comparator #(.Bits(8)) comparator_25 (
    .a(undriven_29), .b({undriven_18, 1'b1}), .eq(comparator_25_eq));  // open: gt, lt
  Comparator #(.Bits(8)) comparator_26 (
    .a(undriven_29), .b({undriven_19, 1'b1}), .eq(comparator_26_eq));  // open: gt, lt
  Comparator #(.Bits(8)) comparator_27 (
    .a(undriven_29), .b({undriven_20, 1'b1}), .eq(comparator_27_eq));  // open: gt, lt
  Comparator #(.Bits(8)) comparator_28 (
    .a(undriven_29), .b({undriven_21, 1'b1}), .eq(comparator_28_eq));  // open: gt, lt
  Comparator #(.Bits(8)) comparator_29 (
    .a(undriven_29), .b({undriven_22, 1'b1}), .eq(comparator_29_eq));  // open: gt, lt
  Bitwise_NOT bitwise_not_1 (.A(register_1_val), .EN(comparator_22_eq), .CLK(shift_register_1_p2), .Q(register_1_q));
  Bitwise_OR bitwise_or_1 (
    .A(register_1_val), .B(register_2_val), .EN(comparator_23_eq), .CLK(shift_register_1_p2));  // open: Q
  Bitwise_AND bitwise_and_1 (
    .A(register_1_val), .B(register_2_val), .EN(comparator_24_eq), .CLK(shift_register_1_p2), .Q(register_1_q));
  Bitwise_XOR bitwise_xor_1 (
    .A(register_1_val), .B(register_2_val), .EN(comparator_25_eq), .CLK(shift_register_1_p2), .Q(register_1_q));
  Binary_NOT binary_not_1 (.A(register_1_val[0]), .EN(comparator_26_eq), .CLK(shift_register_1_p2), .Q(register_1_q));
  Binary_OR binary_or_1 (
    .A(register_1_val[0]), .B(register_2_val[0]), .EN(comparator_27_eq), .CLK(shift_register_1_p2),
    .Q(register_1_q));
  Binary_AND binary_and_1 (
    .A(register_1_val[0]), .B(register_2_val[0]), .EN(comparator_28_eq), .CLK(shift_register_1_p2),
    .Q(register_1_q));
  // Binary_XOR binary_xor_1: pin names not known; wires that end beside it: register_2_val, shift_register_1_p1, shift_register_1_p2, register_1_val, register_2_val, comparator_29_eq, shift_register_1_p2, register_1_q, register_1_q
  // Pins of 1 and 8 bits meet at register_1_val
  // Pins of 1 and 8 bits meet at register_2_val
  // Pins of 1 and 8 bits meet at {undriven_5, 1'b1}
  // Pins of 1 and 8 bits meet at {undriven_6, 1'b1}
  // Pins of 1 and 8 bits meet at {undriven_7, 1'b1}
  // Pins of 1 and 8 bits meet at {undriven_10, 1'b1}
  // Pins of 1 and 8 bits meet at {undriven_11, 1'b1}
  // Pins of 1 and 8 bits meet at {undriven_12, 1'b1}
  // Pins of 1 and 8 bits meet at {undriven_15, 1'b1}
  // Pins of 1 and 8 bits meet at {undriven_16, 1'b1}
  // Pins of 1 and 8 bits meet at {undriven_17, 1'b1}
  // Pins of 1 and 8 bits meet at {undriven_18, 1'b1}

  // Notes on the sheet:
  //   CMD
  //   DAT
  //   CLK
  //   A
  //   B
  //   C
  //   Q
endmodule
