// Digital circuit CPU.dig as structural Verilog
module CPU (
  input  CLR_PC,
  input  STR,
  input  clk
);

  wire alu_1_dat_dis, and_1_out, button_1_out, comparator_1_lt, comparator_2_eq, comparator_3_eq,
       comparator_4_eq, comparator_5_eq, comparator_6_eq, comparator_7_eq, comparator_8_eq, comparator_9_eq,
       comparator_10_eq, comparator_11_eq, comparator_12_eq, diodeforward_1_out, or_1_out;
  wire [3:0] register_2_val, register_2_val_2;
  wire [7:0] counterpreset_1_out, dipswitch_1_out, flash_memory_1_q_cmd, flash_memory_1_q_dat,
       register_1_val, sub_1_s;
  wire [15:0] flash_memory_1_q_adr, programme_counter_1_ln;

  LED led_1 (.in(register_1_val[7]));
  LED led_2 (.in(register_1_val[6]));
  DipSwitch dipswitch_1 (.out(dipswitch_1_out[7]));
  DipSwitch dipswitch_2 (.out(dipswitch_1_out[6]));
  LED led_3 (.in(register_1_val[5]));
  LED led_4 (.in(register_1_val[4]));
  DipSwitch dipswitch_3 (.out(dipswitch_1_out[5]));
  DipSwitch dipswitch_4 (.out(dipswitch_1_out[4]));
  LED led_5 (.in(register_1_val[3]));
  LED led_6 (.in(register_1_val[2]));
  DipSwitch dipswitch_5 (.out(dipswitch_1_out[3]));
  DipSwitch dipswitch_6 (.out(dipswitch_1_out[2]));
  LED led_7 (.in(register_1_val[1]));
  LED led_8 (.in(register_1_val[0]));
  DipSwitch dipswitch_7 (.out(dipswitch_1_out[1]));
  DipSwitch dipswitch_8 (.out(dipswitch_1_out[0]));
  Button button_1 (.out(button_1_out));
  CounterPreset #(.maxValue(65535), .Bits(8), .isProgramCounter("true")) counterpreset_1 (
    .en(1'b1), .C(clk), .dir(1'b0), .in({8{1'b0}}), .ld(1'b0), .clr(1'b0), .out(counterpreset_1_out));  // open: ovf
  Sub #(.Bits(8)) sub_1 (.a(8'h41), .b(8'h1), .c_i(1'b0), .s(sub_1_s));  // open: c_o
  Comparator #(.Bits(8)) comparator_1 (.a(counterpreset_1_out), .b(sub_1_s), .lt(comparator_1_lt));  // open: gt, eq
  and and_1 (and_1_out, comparator_1_lt, clk);
  Comparator #(.Bits(8)) comparator_2 (.a(flash_memory_1_q_cmd), .b(8'h1), .eq(comparator_2_eq));  // open: gt, lt
  Comparator #(.Bits(8)) comparator_3 (.a(flash_memory_1_q_cmd), .b(8'h2), .eq(comparator_3_eq));  // open: gt, lt
  Comparator #(.Bits(8)) comparator_4 (.a(flash_memory_1_q_cmd), .b(8'h3), .eq(comparator_4_eq));  // open: gt, lt
  Comparator #(.Bits(8)) comparator_5 (.a(flash_memory_1_q_cmd), .b(8'h4), .eq(comparator_5_eq));  // open: gt, lt
  Comparator #(.Bits(8)) comparator_6 (.a(flash_memory_1_q_cmd), .b(8'h5), .eq(comparator_6_eq));  // open: gt, lt
  Comparator #(.Bits(8)) comparator_7 (.a(flash_memory_1_q_cmd), .b(8'h6), .eq(comparator_7_eq));  // open: gt, lt
  Comparator #(.Bits(8)) comparator_8 (.a(flash_memory_1_q_cmd), .b(8'h7), .eq(comparator_8_eq));  // open: gt, lt
  Comparator #(.Bits(8)) comparator_9 (.a(flash_memory_1_q_cmd), .b(8'h26), .eq(comparator_9_eq));  // open: gt, lt
  Comparator #(.Bits(8)) comparator_10 (.a(flash_memory_1_q_cmd), .b(8'h27), .eq(comparator_10_eq));  // open: gt, lt
  Comparator #(.Bits(8)) comparator_11 (.a(flash_memory_1_q_cmd), .b(8'h28), .eq(comparator_11_eq));  // open: gt, lt
  Comparator #(.Bits(8)) comparator_12 (.a(flash_memory_1_q_cmd), .b(8'h29), .eq(comparator_12_eq));  // open: gt, lt
  or or_1 (or_1_out, button_1_out, and_1_out);
  DiodeForward diodeforward_1 (.in(comparator_8_eq), .out(diodeforward_1_out));
  DiodeForward diodeforward_2 (.in(comparator_9_eq), .out(diodeforward_1_out));
  DiodeForward diodeforward_3 (.in(comparator_10_eq), .out(diodeforward_1_out));
  DiodeForward diodeforward_4 (.in(comparator_12_eq), .out(diodeforward_1_out));
  PullDown pulldown_1 (.out(diodeforward_1_out));
  Programme_Counter programme_counter_1 (
    .DAT(flash_memory_1_q_dat), .ADR(flash_memory_1_q_adr), .CLK(or_1_out), .JMP(comparator_2_eq),
    .CJP(comparator_3_eq), .CLR(CLR_PC), .LN(programme_counter_1_ln));
  Flash_Memory flash_memory_1 (
    .LN(programme_counter_1_ln), .DAT_dis(diodeforward_1_out), .ADR_dis(comparator_6_eq), .CLK(or_1_out),
    .Q_CMD(flash_memory_1_q_cmd), .Q_DAT(flash_memory_1_q_dat), .Q_ADR(flash_memory_1_q_adr));
  ALU alu_1 (
    .CMD(flash_memory_1_q_cmd), .DAT(flash_memory_1_q_dat), .CLK(or_1_out), .Q(flash_memory_1_q_dat),
    .DAT_dis(alu_1_dat_dis));
  DiodeForward diodeforward_5 (.in(alu_1_dat_dis), .out(diodeforward_1_out));
  DAT_to_ADR_interface dat_to_adr_interface_1 (
    .DAT(flash_memory_1_q_dat), .STR_1(comparator_4_eq), .STR_2(comparator_5_eq), .LD(comparator_6_eq),
    .CLK(or_1_out), .ADR(flash_memory_1_q_adr));
  RAM ram_1 (
    .DAT(flash_memory_1_q_dat), .ADR(flash_memory_1_q_adr), .STR(comparator_7_eq), .LD(comparator_8_eq),
    .CLK(or_1_out), .Q(flash_memory_1_q_dat));
  Register register_1 (
    .D(dipswitch_1_out), .STR(STR), .LD(comparator_9_eq), .CLK(or_1_out), .VAL(register_1_val),
    .Q(flash_memory_1_q_dat));
  Input_Control input_control_1 (.INP(STR), .LD(comparator_10_eq), .CLK(or_1_out), .Q(flash_memory_1_q_dat));
  Register register_2 (
    .D(flash_memory_1_q_dat), .STR(comparator_11_eq), .LD(comparator_12_eq), .CLK(or_1_out),
    .VAL({register_2_val_2, register_2_val}), .Q(flash_memory_1_q_dat));
  Seven_Seg_Hex seven_seg_hex_1 (.d(register_2_val_2), .dp(1'b0));
  Seven_Seg_Hex seven_seg_hex_2 (.d(register_2_val), .dp(1'b0));
  LED led_9 (.in(register_2_val_2[3]));
  LED led_10 (.in(register_2_val_2[2]));
  LED led_11 (.in(register_2_val_2[1]));
  LED led_12 (.in(register_2_val_2[0]));
  LED led_13 (.in(register_2_val[3]));
  LED led_14 (.in(register_2_val[2]));
  LED led_15 (.in(register_2_val[1]));
  LED led_16 (.in(register_2_val[0]));

  // Notes on the sheet:
  //   clk: Hz: 20
  //   CMD
  //   DAT
  //   ADR
  //   CLK
  //   LN: current line of code being executed
  //   DAT_dis
  //   commands requiring the address bus to be disabled:
  //   Bus Transfer:
  //   - load from interface registers
  //   commands requiring the data bus to be disabled:
  //   Storage: 
  //   - load
  //   ALU:
  //   - add
  //   - add with carry
  //   - subtract
  //   incrementor:
  //   - increment
  //   - decrement
  //   logic:
  //   - binary not
  //   - binary or
  //   - binary and
  //   - binary xor
  //   - bitwise not
  //   - bitwise or
  //   - bitwise and
  //   - bitwise xor
  //   a/b/c registers:
  //   - load a
  //   - load b
  //   - load c
  //   compare:
  //   - bigger
  //   - equal
  //   - smaller
  //   flag reg:
  //   - load carry
  //   - load overflow
  //   - load flags
endmodule
