// Digital circuit RAM.dig as structural Verilog
module RAM (
  input  [7:0] DAT,
  input  [15:0] ADR,
  input  STR,
  input  LD,
  input  CLK,
  output [7:0] Q
);

  wire d_ff_1_q, delay_1_out, not_1_out;
  wire [7:0] driver_1_out, register_1_q;

  assign driver_1_out = STR ? DAT : 8'bz;  // Driver driver_1
  not not_1 (not_1_out, CLK);
  D_FF d_ff_1 (.D(LD), .C(not_1_out), .Q(d_ff_1_q));  // open: nQ
  RAMSinglePort #(.AddrBits(16), .Bits(8)) ramsingleport_1 (
    .A(ADR), .str(STR), .C(not_1_out), .ld(d_ff_1_q), .D(driver_1_out));
  Delay delay_1 (.in(d_ff_1_q), .out(delay_1_out));
  Register #(.Bits(8)) register_1 (.D(driver_1_out), .C(delay_1_out), .en(1'b1), .Q(register_1_q));
  assign Q = delay_1_out ? register_1_q : 8'bz;  // Driver driver_2

  // Notes on the sheet:
  //   two subsequent load commands can't be performed,
  //   since the previous address stays buffered.
  //   not a problem, just an observation
  //   (since the data after a load command just persists for
  //   one clock pulse, the first operation would be redundant)
  //   str - store to ram
  //   ld - write to data bus
  //    (output enable)
  //   this is just to replicate the function of the
  //   single port ram we are trying to use, as there
  //   are no bidirectional i/o ports in this 
  //   programme
endmodule
