// Digital circuit Register.dig as structural Verilog
module Register (
  input  [7:0] D,
  input  STR,
  input  LD,
  input  CLK,
  output [7:0] VAL,
  output [7:0] Q
);

  wire d_ff_1_q, delay_1_out, not_1_out;

  Delay delay_1 (.in(STR), .out(delay_1_out));
  not not_1 (not_1_out, CLK);
  Register #(.Bits(8)) register_1 (.D(D), .C(delay_1_out), .en(1'b1), .Q(VAL));
  D_FF d_ff_1 (.D(LD), .C(not_1_out), .Q(d_ff_1_q));  // open: nQ
  assign Q = d_ff_1_q ? VAL : 8'bz;  // Driver driver_1
endmodule
