// Digital circuit Shift Register.dig as structural Verilog
module Shift_Register (
  input  [7:0] A,
  input  STR,
  input  SHR,
  input  SHL,
  input  CLK,
  output [7:0] Q
);

  wire and_1_out;
  wire [7:0] left_out, register_1_q;

  and and_1 (and_1_out, STR, CLK);
  Register #(.Bits(8)) register_1 (.D(A), .C(and_1_out), .en(1'b1), .Q(register_1_q));
  BarrelShifter #(.Bits(8)) left (.in(register_1_q), .shift({3'b000, SHL}), .out(left_out));
  BarrelShifter #(.Bits(8), .direction("right")) right (.in(left_out), .shift({3'b000, SHR}), .out(Q));
endmodule
